// Logisim project logi.circ as structural Verilog
module And (
  input  a,
  input  b,
  output out
);

  wire nand_1_out;

  nand nand_1 (nand_1_out, a, b);
  not not_1 (out, nand_1_out);

  // Notes on the sheet:
  //   outNand
endmodule

module Not (
  input  in,
  output out
);

  nand nand_1 (out, in, in);
endmodule

module Or (
  input  a,
  input  b,
  output out
);

  wire and_out, not_1_out, not_2_out;

  not not_1 (not_1_out, a);
  not not_2 (not_2_out, b);
  and \and  (and_out, not_1_out, not_2_out);
  not not_3 (out, and_out);
endmodule

module Xor (
  input  a,
  input  b,
  output out
);

  wire and_1_out, and_2_out, not_1_out, not_2_out;

  Not not_1 (.in(a), .out(not_1_out));
  Not not_2 (.in(b), .out(not_2_out));
  and and_1 (and_1_out, not_1_out, b);
  and and_2 (and_2_out, a, not_2_out);
  Or or_1 (.a(and_1_out), .b(and_2_out), .out(out));
endmodule

module And_Nand (
  input  a,
  input  b,
  output out_3
);

  wire nand_1_out;

  nand nand_1 (nand_1_out, a, b);
  nand nand_2 (out_3, nand_1_out, nand_1_out);
endmodule

module Not_Nand (
  input  a,
  output out
);

  nand nand_1 (out, a, a);
endmodule

module DMux (
  input  in,
  input  sel,
  output a,
  output b
);

  wire not_1_out;

  not not_1 (not_1_out, sel);
  and and_1 (a, in, not_1_out);
  and and_2 (b, in, sel);
endmodule

module Not16 (
  input  [15:0] in,
  output [15:0] out
);

  wire [15:0] not_2_out;

  assign out = ~in;  // NOT_Gate not_1, 16 bits wide
  not not_2 (not_2_out[0], in[0]);
  not not_3 (not_2_out[1], in[1]);
  not not_4 (not_2_out[2], in[2]);
  not not_5 (not_2_out[3], in[3]);
  not not_6 (not_2_out[4], in[4]);
  not not_7 (not_2_out[5], in[5]);
  not not_8 (not_2_out[6], in[6]);
  not not_9 (not_2_out[7], in[7]);
  not not_10 (not_2_out[8], in[8]);
  not not_11 (not_2_out[9], in[9]);
  not not_12 (not_2_out[10], in[10]);
  not not_13 (not_2_out[11], in[11]);
  not not_14 (not_2_out[12], in[12]);
  not not_15 (not_2_out[13], in[13]);
  not not_16 (not_2_out[14], in[14]);
  not not_17 (not_2_out[15], in[15]);
endmodule

module And16 (
  input  [15:0] a,
  input  [15:0] b,
  output [15:0] out
);

  wire [15:0] nand_1_out;

  assign nand_1_out = ~(a & b);  // NAND_Gate nand_1, 16 bits wide
  assign out = ~nand_1_out;  // NOT_Gate not_1, 16 bits wide

  // Notes on the sheet:
  //   outNand
endmodule

module Or16 (
  input  [15:0] a,
  input  [15:0] b,
  output [15:0] out
);

  wire [15:0] and_out, not_1_out, not_2_out;

  assign not_1_out = ~a;  // NOT_Gate not_1, 16 bits wide
  assign not_2_out = ~b;  // NOT_Gate not_2, 16 bits wide
  assign and_out = not_1_out & not_2_out;  // AND_Gate and, 16 bits wide
  assign out = ~and_out;  // NOT_Gate not_3, 16 bits wide
endmodule

module Mux16 (
  input  [15:0] b,
  input  [15:0] sel,
  input  [15:0] a,
  output [15:0] out
);

  wire [15:0] and_1_out, and_2_out, not_1_out;

  assign and_1_out = b & sel;  // AND_Gate and_1, 16 bits wide
  assign not_1_out = ~sel;  // NOT_Gate not_1, 16 bits wide
  assign and_2_out = not_1_out & a;  // AND_Gate and_2, 16 bits wide
  assign out = and_1_out | and_2_out;  // OR_Gate or_1, 16 bits wide
endmodule

module Mux (
  input  b,
  input  sel,
  input  a,
  output out
);

  wire and_1_out, and_2_out, not_1_out;

  and and_1 (and_1_out, b, sel);
  not not_1 (not_1_out, sel);
  and and_2 (and_2_out, not_1_out, a);
  or or_1 (out, and_1_out, and_2_out);
endmodule

module Or8way (
  input  [7:0] in,
  output out
);

  or or_1 (out, in[0], in[1], in[2], in[3], in[4], in[5], in[6], in[7]);
endmodule

module Mux4way16 (
  input  [15:0] a,
  input  [15:0] b,
  input  [15:0] sel_1,
  input  [15:0] c,
  input  [15:0] d,
  input  [15:0] sel_2,
  output [15:0] out
);

  wire [15:0] ab_out, cd_out;

  Mux16 ab (.b(a), .sel(b), .a(sel_1), .out(ab_out));
  Mux16 cd (.b(sel_1), .sel(c), .a(d), .out(cd_out));
  Mux16 abcd (.b(ab_out), .sel(cd_out), .a(sel_2), .out(out));
endmodule

module Mux8way16 (
  input  [15:0] a,
  input  [15:0] b,
  input  [15:0] c,
  input  [15:0] d,
  input  [15:0] sel_1,
  input  [15:0] sel_2,
  input  [15:0] sel_3,
  input  [15:0] e,
  input  [15:0] f,
  input  [15:0] g,
  input  [15:0] h,
  output [15:0] out
);

  wire [15:0] ab_out, abcd_out, cd_out, ef_out, efgh_out, gh_out;

  Mux16 ab (.b(a), .sel(b), .a(sel_1), .out(ab_out));
  Mux16 cd (.b(sel_1), .sel(c), .a(d), .out(cd_out));
  Mux16 ef (.b(e), .sel(f), .a(sel_1), .out(ef_out));
  Mux16 gh (.b(sel_1), .sel(g), .a(h), .out(gh_out));
  Mux16 abcd (.b(ab_out), .sel(cd_out), .a(sel_2), .out(abcd_out));
  Mux16 efgh (.b(sel_2), .sel(ef_out), .a(gh_out), .out(efgh_out));
  Mux16 abcd_2 (.b(abcd_out), .sel(sel_3), .a(efgh_out));  // open: out
endmodule

module Sumador_parcial (
  input  a,
  input  b,
  output sum,
  output carry
);

  xor xor_1 (sum, a, b);
  and and_1 (carry, a, b);
endmodule

module Sumador_completo (
  input  a,
  input  b,
  input  Carry_in,
  output sum,
  output carry
);

  wire and_1_out, and_2_out, xor_1_out;

  xor xor_1 (xor_1_out, a, b);
  and and_1 (and_1_out, a, b);
  xor xor_2 (sum, xor_1_out, Carry_in);
  and and_2 (and_2_out, Carry_in, xor_1_out);
  or or_1 (carry, and_1_out, and_2_out);
endmodule

module Add16 (
  input  [15:0] a,
  input  [15:0] b,
  output [15:0] out,
  output out_4
);

  wire sumador_completo_1_carry, sumador_completo_2_carry, sumador_completo_3_carry,
       sumador_completo_4_carry, sumador_completo_5_carry, sumador_completo_6_carry,
       sumador_completo_7_carry, sumador_completo_8_carry, sumador_completo_9_carry,
       sumador_completo_10_carry, sumador_completo_11_carry, sumador_completo_12_carry,
       sumador_completo_13_carry, sumador_completo_14_carry, sumador_parcial_1_carry;

  Sumador_parcial sumador_parcial_1 (.a(a[0]), .b(b[0]), .sum(out[0]), .carry(sumador_parcial_1_carry));
  Sumador_completo sumador_completo_1 (
    .a(a[1]), .b(b[1]), .Carry_in(sumador_parcial_1_carry), .sum(out[1]), .carry(sumador_completo_1_carry));
  Sumador_completo sumador_completo_2 (
    .a(a[2]), .b(b[2]), .Carry_in(sumador_completo_1_carry), .sum(out[2]), .carry(sumador_completo_2_carry));
  Sumador_completo sumador_completo_3 (
    .a(a[3]), .b(b[3]), .Carry_in(sumador_completo_2_carry), .sum(out[3]), .carry(sumador_completo_3_carry));
  Sumador_completo sumador_completo_4 (
    .a(a[4]), .b(b[4]), .Carry_in(sumador_completo_3_carry), .sum(out[4]), .carry(sumador_completo_4_carry));
  Sumador_completo sumador_completo_5 (
    .a(a[5]), .b(b[5]), .Carry_in(sumador_completo_4_carry), .sum(out[5]), .carry(sumador_completo_5_carry));
  Sumador_completo sumador_completo_6 (
    .a(a[6]), .b(b[6]), .Carry_in(sumador_completo_5_carry), .sum(out[6]), .carry(sumador_completo_6_carry));
  Sumador_completo sumador_completo_7 (
    .a(a[7]), .b(b[7]), .Carry_in(sumador_completo_6_carry), .sum(out[7]), .carry(sumador_completo_7_carry));
  Sumador_completo sumador_completo_8 (
    .a(a[8]), .b(b[8]), .Carry_in(sumador_completo_7_carry), .sum(out[8]), .carry(sumador_completo_8_carry));
  Sumador_completo sumador_completo_9 (
    .a(a[9]), .b(b[9]), .Carry_in(sumador_completo_8_carry), .sum(out[9]), .carry(sumador_completo_9_carry));
  Sumador_completo sumador_completo_10 (
    .a(a[10]), .b(b[10]), .Carry_in(sumador_completo_9_carry), .sum(out[10]),
    .carry(sumador_completo_10_carry));
  Sumador_completo sumador_completo_11 (
    .a(a[11]), .b(b[11]), .Carry_in(sumador_completo_10_carry), .sum(out[11]),
    .carry(sumador_completo_11_carry));
  Sumador_completo sumador_completo_12 (
    .a(a[12]), .b(b[12]), .Carry_in(sumador_completo_11_carry), .sum(out[12]),
    .carry(sumador_completo_12_carry));
  Sumador_completo sumador_completo_13 (
    .a(a[13]), .b(b[13]), .Carry_in(sumador_completo_12_carry), .sum(out[13]),
    .carry(sumador_completo_13_carry));
  Sumador_completo sumador_completo_14 (
    .a(a[14]), .b(b[14]), .Carry_in(sumador_completo_13_carry), .sum(out[14]),
    .carry(sumador_completo_14_carry));
  Sumador_completo sumador_completo_15 (
    .a(a[15]), .b(b[15]), .Carry_in(sumador_completo_14_carry), .sum(out[15]), .carry(out_4));
endmodule

module reloj (
  input  in,
  input  load,
  output out
);

  wire clock_1_out;

  Clock clock_1 (.out(clock_1_out));
  D_Flip_Flop d_ff_1 (.clk(clock_1_out), .D(in), .Q(out), .en(load));  // open: Qn, preset, reset
endmodule

module Bit (
  input  in,
  input  load,
  output out
);

  wire clock_1_out, multiplexer_1_out;

  Clock clock_1 (.out(clock_1_out));
  Multiplexer multiplexer_1 (.in0(out), .in1(in), .out(multiplexer_1_out), .sel(load));  // open: en
  D_Flip_Flop d_ff_1 (.clk(clock_1_out), .D(multiplexer_1_out), .Q(out));  // open: Qn, preset, en, reset
endmodule

module Register (
  input  [15:0] load,
  input  [15:0] in,
  output [15:0] out
);

  Bit bit_1 (.in(in[0]), .load(load[0]), .out(out[0]));
  Bit bit_2 (.in(in[2]), .load(load[2]), .out(out[2]));
  Bit bit_3 (.in(in[4]), .load(load[4]), .out(out[4]));
  Bit bit_4 (.in(in[6]), .load(load[6]), .out(out[6]));
  Bit bit_5 (.in(in[8]), .load(load[8]), .out(out[8]));
  Bit bit_6 (.in(in[10]), .load(load[10]), .out(out[10]));
  Bit bit_7 (.in(in[12]), .load(load[12]), .out(out[12]));
  Bit bit_8 (.in(in[14]), .load(load[14]), .out(out[14]));
  Bit bit_9 (.in(in[1]), .load(load[1]), .out(out[1]));
  Bit bit_10 (.in(in[3]), .load(load[3]), .out(out[3]));
  Bit bit_11 (.in(in[5]), .load(load[5]), .out(out[5]));
  Bit bit_12 (.in(in[7]), .load(load[7]), .out(out[7]));
  Bit bit_13 (.in(in[9]), .load(load[9]), .out(out[9]));
  Bit bit_14 (.in(in[11]), .load(load[11]), .out(out[11]));
  Bit bit_15 (.in(in[13]), .load(load[13]), .out(out[13]));
  Bit bit_16 (.in(in[15]), .load(load[15]), .out(out[15]));
endmodule

module Dmux4Way (
  input  in,
  input  sel_2,
  input  sel_1,
  output a,
  output b,
  output c,
  output d
);

  wire demultiplexer_1_out0, demultiplexer_1_out1;

  Demultiplexer demultiplexer_1 (
    .out0(demultiplexer_1_out0), .out1(demultiplexer_1_out1), .in(in), .sel(sel_1));  // open: en
  Demultiplexer demultiplexer_2 (.out0(a), .out1(b), .in(demultiplexer_1_out0), .sel(sel_2));  // open: en
  Demultiplexer demultiplexer_3 (.out0(c), .out1(d), .in(demultiplexer_1_out1), .sel(sel_2));  // open: en
endmodule

module Dmux8Way (
  input  in,
  input  sel_1,
  input  sel_0,
  input  sel_2,
  output a,
  output b,
  output c,
  output d,
  output e,
  output f,
  output g,
  output h
);

  wire demultiplexer_1_out0, demultiplexer_1_out1, demultiplexer_2_out0, demultiplexer_2_out1,
       demultiplexer_3_out0, demultiplexer_3_out1;

  Demultiplexer demultiplexer_1 (
    .out0(demultiplexer_1_out0), .out1(demultiplexer_1_out1), .in(in), .sel(sel_2));  // open: en
  Demultiplexer demultiplexer_2 (
    .out0(demultiplexer_2_out0), .out1(demultiplexer_2_out1), .in(demultiplexer_1_out0), .sel(sel_1));  // open: en
  Demultiplexer demultiplexer_3 (
    .out0(demultiplexer_3_out0), .out1(demultiplexer_3_out1), .in(demultiplexer_1_out1), .sel(sel_1));  // open: en
  Demultiplexer demultiplexer_4 (.out0(c), .out1(d), .in(demultiplexer_2_out1), .sel(sel_0));  // open: en
  Demultiplexer demultiplexer_5 (.out0(e), .out1(f), .in(demultiplexer_3_out0), .sel(sel_0));  // open: en
  Demultiplexer demultiplexer_6 (.out0(a), .out1(b), .in(demultiplexer_2_out0), .sel(sel_0));  // open: en
  Demultiplexer demultiplexer_7 (.out0(g), .out1(h), .in(demultiplexer_3_out1), .sel(sel_0));  // open: en
endmodule

module Inc16 (
  input  [15:0] a,
  output [15:0] out
);

  Add16 add16_1 (.a(a), .out(out), .b(16'h1));  // open: out_4
endmodule
